# Fritzing sketch roboscan-wiring (saved by Fritzing 0.9.4)

parts:
  Raspberry_Pi_1 = Raspberry Pi 3 [part_number=RPI-3-V1.2]
  BREAKOUT1 = ULN2003A breakout board
  MOTOR1 = 28BYJ-48 Stepper Motor
  LED2 = LED - 3W Aluminum PCB
  LED_Driver1 = 1w_led_driver_350ma_pmw [package="DIP (Dual Inline) [THT]"]
  C1 = Electrolytic Capacitor [capacitance=47µF voltage=50V package="200 mil [THT, electrolytic]"]

nets:
  N1: Raspberry_Pi_1.GPIO5, BREAKOUT1.In_1
  N2: Raspberry_Pi_1.GPIO6, BREAKOUT1.In_2
  N3: Raspberry_Pi_1.GPIO13, BREAKOUT1.In_3
  N4: Raspberry_Pi_1.GPIO19, BREAKOUT1.In_4
  N5: Raspberry_Pi_1.GND, BREAKOUT1.0V, LED_Driver1.VIN-
  N6: Raspberry_Pi_1.GPIO18, LED_Driver1.PMW
  5V: Raspberry_Pi_1.5V, BREAKOUT1.+5V, LED_Driver1.VIN+
  N7: BREAKOUT1.RED_wire, MOTOR1.RED
  N8: BREAKOUT1.ORANGE_wire, MOTOR1.ORANGE
  N9: BREAKOUT1.YELLOW_wire, MOTOR1.YELLOW
  N10: BREAKOUT1.PINK_wire, MOTOR1.PINK
  N11: BREAKOUT1.BLUE_wire, MOTOR1.BLUE
  N12: LED2.anode, LED_Driver1.LED+, C1.+
  N13: LED2.cathode, LED_Driver1.LED-, C1.-

custom parts:
  ULN2003A breakout board: ULN2003A 7-way Darlington Transistor Driver on breakoutboard
  LED - 3W Aluminum PCB: Description: So much power and light from such a small package. This 5 pack of red 3 Watt aluminum backed PCBs is sure to shed a lot of light on any project you add it to. These LEDs act as any other LED except these little guys require much more power while delivering a light as intense of a thousand suns going super nova (this is an exaggeration but you know what we mean)! Each LED in the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
  1w_led_driver_350ma_pmw: 1W LED Driver 350ma PMW
